# Fritzing sketch rpm-01 (saved by Fritzing 0.9.3b)
circuit board: 8.46667cm x 5.64444cm
breadboards: 1

parts:
  LCD1 = LCD screen
  Part1 = Arduino Nano (Rev3.0)
  R1 = Trimmer Potentiometer [maximum_resistance=10kΩ package=THT]
  R2 = Resistor [tolerance=±5% resistance=220 package=THT]
  Power_plug1 = Power plug
  U2 = CNZ1120 [package=cnz1120]
  R3 = Resistor [tolerance=±5% resistance=220 package=THT]
  R4 = Resistor [tolerance=±5% resistance=330 package=THT]

nets:
  GND: LCD1.VSS, LCD1.R/W, Part1.GND, R1.leg2, R2.Pin_1, Power_plug1.GND, U2.2, R4.Pin_0
  VDD: LCD1.VDD, LCD1.LED+, Part1.5V, R1.leg1, Power_plug1.VCC, U2.3, R3.Pin_0
  N1: LCD1.V0, R1.wiper
  N2: LCD1.RS, Part1.D12/MISO
  N3: LCD1.E, Part1.D11/MOSI
  N4: LCD1.DB4, Part1.D7
  N5: LCD1.DB5, Part1.D8
  N6: LCD1.DB6, Part1.D9
  N7: LCD1.DB7, Part1.D10
  N8: LCD1.LED-, R2.Pin_0
  N9: Part1.D2, U2.4, R4.Pin_1
  N10: U2.1, R3.Pin_1
