# Fritzing sketch sensDuino2 (saved by Fritzing 0.9.3b)
circuit board: 8.46667cm x 5.64444cm

parts:
  Part1 = BME280 Breakout
  Part2 = Arduino Nano (Rev3.0)
  U1 = ESP8266 WiFi Module [part_number=ESP8266]
  Part3 = Logic Level Converter
  RHT1 = Humidity and Temperature Sensor RHT03
  R1 = PHOTOCELL [package=photocell-kit]
  IC2 = Voltage Regulator [package=78xxl]
  J1 = Power Jack [package=power_jack_pth]
  C2 = Electrolytic Capacitor [capacitance=1µF package="100 mil [THT, electrolytic]"]  # not connected
  C3 = Electrolytic Capacitor [capacitance=1µF package="100 mil [THT, electrolytic]"]  # not connected
  R3 = Resistor [tolerance=±5% resistance=330 package=THT]
  R4 = Resistor [tolerance=±5% resistance=330 package=THT]
  R5 = Resistor [tolerance=±5% resistance=330 package=THT]
  R6 = Resistor [tolerance=±5% resistance=330 package=THT]
  R7 = Resistor [tolerance=±5% resistance=330 package=THT]
  R8 = Resistor [tolerance=±5% resistance=330 package=THT]
  R9 = Resistor [tolerance=±5% resistance=330 package=THT]
  R10 = Resistor [tolerance=±5% resistance=330 package=THT]
  J2 = shrouded pin header, 16 pins [form="♂ (shrouded male)"]
  R11 = Resistor [tolerance=±5% resistance=330 package=THT]
  R12 = Resistor [tolerance=±5% resistance=330 package=THT]
  R13 = Resistor [tolerance=±5% resistance=330 package=THT]
  R14 = Resistor [tolerance=±5% resistance=330 package=THT]
  R15 = Resistor [tolerance=±5% resistance=330 package=THT]
  R16 = Resistor [tolerance=±5% resistance=330 package=THT]
  R17 = Resistor [tolerance=±5% resistance=330 package=THT]
  R18 = Resistor [tolerance=±5% resistance=330 package=THT]
  R19 = Resistor [tolerance=±5% resistance=4.7k package=THT]
  R20 = Resistor [tolerance=±5% resistance=4.7k package=THT]
  S1 = Reed switch [package=THT]  # not connected
  S2 = Reed switch [package=THT]
  J3 = shrouded pin header, 16 pins [form="♂ (shrouded male)"]
  S3 = Reed switch [package=THT]
  S4 = Reed switch [package=THT]
  S5 = Reed switch [package=THT]
  S6 = Reed switch [package=THT]
  S7 = Reed switch [package=THT]
  S8 = Reed switch [package=THT]
  S9 = Reed switch [package=THT]
  S10 = Reed switch [package=THT]  # not connected
  S11 = Reed switch [package=THT]  # not connected
  S12 = Reed switch [package=THT]  # not connected
  J4 = Power Jack [package=power_jack_pth]
  U5 = V_REG_LD1117VXX [package=78xxl]
  U6 = Sharp PC847X [package=THT]
  U7 = Sharp PC847X [package=THT]

nets:
  GND: Part1.GND, Part2.GND, U1.GND, Part3.GND, RHT1.GND_2, R17.Pin_1
  N1: Part1.SDI/SDA, Part2.A4
  N2: Part1.SCK/SCL, Part2.A5
  N3: Part2.D2, R11.Pin_0, U6.Pin_16
  N4: Part2.D3, R18.Pin_0, U6.Pin_14
  N5: Part2.D4, R17.Pin_0, U6.Pin_12
  N6: Part2.D5, R16.Pin_0, U6.Pin_10
  N7: Part2.D6, R15.Pin_0, U7.Pin_16
  N8: Part2.D7, R14.Pin_0, U7.Pin_14
  N9: Part2.D8, R13.Pin_0, U7.Pin_12
  N10: Part2.D9, R12.Pin_0, U7.Pin_10
  N11: Part2.D10, Part3.TX_HV
  N12: Part2.D11/MOSI, Part3.RX_HV
  N13: Part2.D12/MISO, RHT1.Data-signal, R19.Pin_0
  VIN: Part2.VIN, RHT1.Vcc, R1.P$1, R19.Pin_1
  N14: Part2.A0, R1.P$2, R20.Pin_0
  N15: U1.RXD, Part3.RX_LV
  N16: U1.VCC, U1.RST, U1.CH_PD, Part3.LV, U5.OUT
  N17: U1.TXD, Part3.TX_LV
  N18: IC2.GND, J1.GNDBREAK
  N19: IC2.IN, J1.PWR
  N20: R3.Pin_0, J2.pin8
  N21: R4.Pin_0, J2.pin7
  N22: R5.Pin_0, J2.pin6
  N23: R6.Pin_0, J2.pin5
  N24: R7.Pin_0, J2.pin4
  N25: R8.Pin_0, J2.pin3
  N26: R9.Pin_0, J2.pin1
  N27: R10.Pin_0, J2.pin2
  N28: J2.pin9, J2.pin10, J2.pin11, J2.pin12, J2.pin13, J2.pin14, J2.pin15, J2.pin16
  N29: S2.pin_1, S3.pin_1, S4.pin_1, S5.pin_1, S6.pin_1, S7.pin_1
  N30: S2.pin_2, J3.pin9
  N31: J3.pin1, J4.GNDBREAK
  N32: J3.pin2, J3.pin3, J3.pin4, J3.pin5, J3.pin6, J3.pin7, J3.pin8
  N33: J3.pin10, S3.pin_2
  N34: J3.pin11, S4.pin_2
  N35: J3.pin12, S5.pin_2
  N36: J3.pin13, S6.pin_2
  N37: J3.pin14, S7.pin_2
  N38: J3.pin15, S8.pin_2
  N39: J3.pin16, S9.pin_2
  N40: S8.pin_1, S9.pin_1
  N41: U6.Pin_9, U7.Pin_13, U7.Pin_15
  N42: U6.Pin_11, U6.Pin_13, U6.Pin_15
  N43: U7.Pin_9, U7.Pin_11

notes:
  DHT22
  Arduino Nano
  USB
  LDR
  ESP-01 (esp8266)
  LM1117 - 3.3v
  uA7805 - 5v
  BMP280
  3.3 <-> 5
  LTV847
  5-15v
  5v

custom parts:
  ESP8266 WiFi Module: Generic WiFi Module based on the ESP8266 with onboard PCB antenna and UART communications
